// Logisim project FINAL CIRCUIT.circ as structural Verilog: 2 circuits, main circuit 1
module _1 (
  output [3:0] INPUT_DISPLAY,
  output [4:0] out_2
);

  wire and_1_out, and_2_out, clock_1_out, comparator_1_eq, comparator_1_lt, comparator_2_eq, comparator_4_eq,
       comparator_5_eq, comparator_5_lt, comparator_7_eq, comparator_8_eq, comparator_9_eq, comparator_10_eq,
       comparator_11_eq, comparator_12_eq, counter_1_carry, d_ff_1_q, DELETE_out, ENTER_out,
       led_connector_1_out_2, led_connector_1_out_3, led_connector_1_out_4, led_connector_1_out_5,
       led_connector_1_out_6, led_connector_2_out_2, led_connector_2_out_3, led_connector_2_out_4,
       led_connector_2_out_5, led_connector_2_out_6, led_connector_3_out_2, led_connector_3_out_3,
       led_connector_3_out_4, led_connector_3_out_5, led_connector_3_out_6, led_connector_4_out_2,
       led_connector_4_out_3, led_connector_4_out_4, led_connector_4_out_5, led_connector_4_out_6,
       led_connector_5_out_2, led_connector_5_out_3, led_connector_5_out_4, led_connector_5_out_5,
       led_connector_5_out_6, not_1_out, or_4_out, or_6_out, pull_resistor_1_node, pull_resistor_2_node,
       pull_resistor_3_node, pull_resistor_4_node, pull_resistor_5_node, pull_resistor_6_node;
  wire [2:0] adder_1_out, counter_1_q;
  wire [3:0] _0_to_9_out, A_to_F_out;
  wire [3:3] comparator_3_eq, or_1_out, or_2_out, or_3_out;
  wire [4:0] and_3_out, C1_out, C2_out, C3_out, C4_out, C5_out, InV_out, register_1_q, rom_1_data,
       rom_2_data, rom_3_data, rom_4_data, rom_5_data;
  wire [4:4] comparator_6_eq, comparator_13_eq, d_ff_2_q, d_ff_3_q, d_ff_4_q, d_ff_5_q, d_ff_6_q;
  wire [6:0] keyboard_1_data;

  Keyboard #(.buflen(1)) keyboard_1 (
    .clk(counter_1_carry), .clr(DELETE_out), .data(keyboard_1_data));  // open: re, avail
  Comparator #(.width(4), .mode("unsigned")) comparator_1 (
    .a(keyboard_1_data[3:0]), .b(4'b0110), .eq(comparator_1_eq), .lt(comparator_1_lt));  // open: gt
  Comparator #(.width(3), .mode("unsigned")) comparator_2 (
    .a(keyboard_1_data[6:4]), .b(3'b110), .eq(comparator_2_eq));  // open: gt, lt
  Button ENTER (.out(ENTER_out));
  Button DELETE (.out(DELETE_out));
  Comparator #(.width(3), .mode("unsigned")) comparator_3 (
    .a(keyboard_1_data[6:4]), .b(3'b011), .eq(comparator_3_eq[3]));  // open: gt, lt
  Comparator #(.width(3), .mode("unsigned")) comparator_4 (
    .a(keyboard_1_data[6:4]), .b(3'b100), .eq(comparator_4_eq));  // open: gt, lt
  or or_1 (or_1_out[3], comparator_1_eq, comparator_1_lt);
  Comparator #(.width(4), .mode("unsigned")) comparator_5 (
    .a(keyboard_1_data[3:0]), .b(4'b1001), .eq(comparator_5_eq), .lt(comparator_5_lt));  // open: gt
  Adder #(.width(3)) adder_1 (.a(keyboard_1_data[2:0]), .b(3'b001), .out(adder_1_out));  // open: cin, cout
  or or_2 (or_2_out[3], comparator_5_eq, comparator_5_lt);
  or or_3 (or_3_out[3], comparator_4_eq, comparator_2_eq);
  and and_1 (and_1_out, comparator_3_eq[3], or_2_out[3]);
  and and_2 (and_2_out, or_3_out[3], or_1_out[3]);
  assign _0_to_9_out = {4{or_2_out[3]}} & keyboard_1_data[3:0] & {4{comparator_3_eq[3]}};  // AND_Gate _0_to_9, 4 bits wide
  assign INPUT_DISPLAY = _0_to_9_out | A_to_F_out;  // OR_Gate V, 4 bits wide
  assign A_to_F_out = {4{or_3_out[3]}} & {4{or_1_out[3]}} & {1'b1, adder_1_out};  // AND_Gate A_to_F, 4 bits wide
  not not_1 (not_1_out, ENTER_out);
  Clock clock_1 (.out(clock_1_out));
  or or_4 (or_4_out, and_1_out, and_2_out);
  assign InV_out = 5'b10000 & {5{comparator_13_eq[4]}};  // AND_Gate InV, 5 bits wide
  TTY #(.rows(2), .cols(16)) tty_1 (.data(keyboard_1_data), .clk(counter_1_carry));  // open: we, clr
  Counter #(.width(3), .max('h5)) counter_1 (
    .load(1'b0), .count(1'b1), .Q(counter_1_q), .carry(counter_1_carry), .clk(clock_1_out), .clr(or_6_out));  // open: D
  assign out_2 = InV_out | {1'b0, INPUT_DISPLAY};  // OR_Gate or_5, 5 bits wide
  Comparator #(.width(1), .mode("unsigned")) comparator_6 (
    .a(or_4_out), .b(1'b0), .eq(comparator_6_eq[4]));  // open: gt, lt
  Register #(.width(5)) register_1 (.D(out_2), .en(1'b1), .Q(register_1_q), .clk(not_1_out), .clr(ENTER_out));
  or or_6 (or_6_out, ENTER_out, d_ff_1_q);
  Comparator #(.width(3), .mode("unsigned")) comparator_7 (
    .a(counter_1_q), .b(3'b000), .eq(comparator_7_eq));  // open: gt, lt
  Pull_Resistor #(.pull(1)) pull_resistor_1 (.node(pull_resistor_1_node));
  Comparator #(.width(3), .mode("unsigned")) comparator_8 (
    .a(counter_1_q), .b(3'b001), .eq(comparator_8_eq));  // open: gt, lt
  Pull_Resistor #(.pull(1)) pull_resistor_2 (.node(pull_resistor_2_node));
  Comparator #(.width(3), .mode("unsigned")) comparator_9 (
    .a(counter_1_q), .b(3'b010), .eq(comparator_9_eq));  // open: gt, lt
  Pull_Resistor #(.pull(1)) pull_resistor_3 (.node(pull_resistor_3_node));
  Comparator #(.width(3), .mode("unsigned")) comparator_10 (
    .a(counter_1_q), .b(3'b011), .eq(comparator_10_eq));  // open: gt, lt
  Pull_Resistor #(.pull(1)) pull_resistor_4 (.node(pull_resistor_4_node));
  Comparator #(.width(3), .mode("unsigned")) comparator_11 (
    .a(counter_1_q), .b(3'b100), .eq(comparator_11_eq));  // open: gt, lt
  Pull_Resistor #(.pull(1)) pull_resistor_5 (.node(pull_resistor_5_node));
  Comparator #(.width(3), .mode("unsigned")) comparator_12 (
    .a(counter_1_q), .b(3'b101), .eq(comparator_12_eq));  // open: gt, lt
  Pull_Resistor #(.pull(1)) pull_resistor_6 (.node(pull_resistor_6_node));
  assign and_3_out = {5{comparator_6_eq[4]}} & 5'b10000;  // AND_Gate and_3, 5 bits wide
  Comparator #(.width(5), .mode("unsigned")) comparator_13 (
    .a(and_3_out), .b(5'b10000), .eq(comparator_13_eq[4]));  // open: gt, lt
  D_Flip_Flop d_ff_1 (
    .clk(comparator_7_eq), .D(pull_resistor_1_node), .Q(d_ff_1_q), .en(1'b1), .reset(ENTER_out));  // open: Qn, preset
  D_Flip_Flop d_ff_2 (
    .clk(comparator_8_eq), .D(pull_resistor_2_node), .Q(d_ff_2_q[4]), .en(1'b1), .reset(ENTER_out));  // open: Qn, preset
  D_Flip_Flop d_ff_3 (
    .clk(comparator_9_eq), .D(pull_resistor_3_node), .Q(d_ff_3_q[4]), .en(1'b1), .reset(ENTER_out));  // open: Qn, preset
  D_Flip_Flop d_ff_4 (
    .clk(comparator_10_eq), .D(pull_resistor_4_node), .Q(d_ff_4_q[4]), .en(1'b1), .reset(ENTER_out));  // open: Qn, preset
  D_Flip_Flop d_ff_5 (
    .clk(comparator_11_eq), .D(pull_resistor_5_node), .Q(d_ff_5_q[4]), .en(1'b1), .reset(ENTER_out));  // open: Qn, preset
  D_Flip_Flop d_ff_6 (
    .clk(comparator_12_eq), .D(pull_resistor_6_node), .Q(d_ff_6_q[4]), .en(1'b1), .reset(ENTER_out));  // open: Qn, preset
  ROM #(.addrWidth(5), .dataWidth(5)) rom_1 (.addr(register_1_q), .data(rom_1_data));  // open: sel
  ROM #(.addrWidth(5), .dataWidth(5)) rom_2 (.addr(register_1_q), .data(rom_2_data));  // open: sel
  assign C1_out = rom_1_data & {5{d_ff_2_q[4]}};  // AND_Gate C1, 5 bits wide
  assign C2_out = rom_2_data & {5{d_ff_3_q[4]}};  // AND_Gate C2, 5 bits wide
  assign C3_out = rom_3_data & {5{d_ff_4_q[4]}};  // AND_Gate C3, 5 bits wide
  assign C4_out = rom_4_data & {5{d_ff_5_q[4]}};  // AND_Gate C4, 5 bits wide
  assign C5_out = rom_5_data & {5{d_ff_6_q[4]}};  // AND_Gate C5, 5 bits wide
  LED led_1 (.in(led_connector_2_out_2));
  LED led_2 (.in(led_connector_2_out_3));
  LED_Connector led_connector_1 (
    .out_2(led_connector_1_out_2), .out_3(led_connector_1_out_3), .in_1(C2_out),
    .out_4(led_connector_1_out_4), .out_5(led_connector_1_out_5), .out_6(led_connector_1_out_6));
  LED_Connector led_connector_2 (
    .out_2(led_connector_2_out_2), .out_3(led_connector_2_out_3), .in_1(C1_out),
    .out_4(led_connector_2_out_4), .out_5(led_connector_2_out_5), .out_6(led_connector_2_out_6));
  LED led_3 (.in(led_connector_2_out_4));
  LED led_4 (.in(led_connector_2_out_5));
  LED led_5 (.in(led_connector_2_out_6));
  LED led_6 (.in(led_connector_3_out_2));
  LED led_7 (.in(led_connector_1_out_2));
  LED led_8 (.in(led_connector_4_out_2));
  LED led_9 (.in(led_connector_3_out_3));
  LED led_10 (.in(led_connector_4_out_3));
  LED led_11 (.in(led_connector_1_out_3));
  LED_Connector led_connector_3 (
    .out_2(led_connector_3_out_2), .out_3(led_connector_3_out_3), .in_1(C4_out),
    .out_4(led_connector_3_out_4), .out_5(led_connector_3_out_5), .out_6(led_connector_3_out_6));
  LED_Connector led_connector_4 (
    .out_2(led_connector_4_out_2), .out_3(led_connector_4_out_3), .in_1(C3_out),
    .out_4(led_connector_4_out_4), .out_5(led_connector_4_out_5), .out_6(led_connector_4_out_6));
  LED led_12 (.in(led_connector_3_out_4));
  LED led_13 (.in(led_connector_4_out_4));
  LED led_14 (.in(led_connector_1_out_4));
  LED led_15 (.in(led_connector_1_out_5));
  LED led_16 (.in(led_connector_3_out_5));
  LED led_17 (.in(led_connector_4_out_5));
  LED led_18 (.in(led_connector_4_out_6));
  LED led_19 (.in(led_connector_3_out_6));
  LED led_20 (.in(led_connector_1_out_6));
  ROM #(.addrWidth(5), .dataWidth(5)) rom_3 (.addr(register_1_q), .data(rom_3_data));  // open: sel
  LED led_21 (.in(led_connector_5_out_2));
  LED led_22 (.in(led_connector_5_out_3));
  LED_Connector led_connector_5 (
    .out_2(led_connector_5_out_2), .out_3(led_connector_5_out_3), .in_1(C5_out),
    .out_4(led_connector_5_out_4), .out_5(led_connector_5_out_5), .out_6(led_connector_5_out_6));
  LED led_23 (.in(led_connector_5_out_4));
  LED led_24 (.in(led_connector_5_out_5));
  LED led_25 (.in(led_connector_5_out_6));
  ROM #(.addrWidth(5), .dataWidth(5)) rom_4 (.addr(register_1_q), .data(rom_4_data));  // open: sel
  ROM #(.addrWidth(5), .dataWidth(5)) rom_5 (.addr(register_1_q), .data(rom_5_data));  // open: sel

  // Notes on the sheet:
  //   ^
  //   |
  //   |
  //   --->
  //   INPUT
  //   KEYBOARD
  //   (FOR GIVING INPUT)
  //   011
  //   100
  //   110
  //   (FOR LETTING THE INPUT ENTERED ON 
  //   KEYBOARD TO PASS ON TO THE CIRCUIT)
  //   (FOR LETTING USER TO
  //   DELETE THE INPUT SUPPLIED)
  //   ASCII TO HEXADECIMAL CONVERSION CIRCUIT DESIGN
  //   ---------------------------------------------------------------------------------------
  //   (CONTROL OF KEYBOARD'C CLOCK BY COUNTER)
  //   ^
  //   |
  //   |
  //   |
  //   |
  //   -
  //   |
  //   |
  //   MOD-6 COUNTER
  //   ENABLE CIRCUIT DESIGN
  //   (FOR LEFT TO RIGHT IMPLEMENTATION)
  //   -------------------------------------------------------------------------------------------------------------------------------------------------------------------------------
  //   (SIMULATION PURPOSE)
  //   REGISTER
  //   -------------------------------------------------------------------------------------------------------------------------------------------------------------------------------
  //   -------------------------------------------------------------------------------------------------------------------------------------------------------------------------------
  //   -------------------------------------------------------------------------------------------------------------------------------------------------------------------------------
  //   MEMORY ALLOTMENT
  //   ROM FOR COLUMN 1
  //   (FOR COLUMN WISE IMPLEMENTATION)
  //   contents of rom_1 (hex, n*v repeats v):
  //   e 5 9 a 1c 1d e 10 a 8 7 1f e 1f 1f 1f
  //   En Col-1 select
  //   En Col-2 select
  //   En Col-3 select
  //   En Col-4 select
  //   En Col-5 select
  //   <--------
  //   CIRCUIT
  //   DESIGN
  //   FOR
  //   INVALID 
  //   INPUTS
  //   <--------
  //   |
  //   |
  //   |
  //   -------------------------------------------------------------------------------------------------------------------------------------------------------------------------------
  //   contents of rom_2 (hex, n*v repeats v):
  //   11 9 11 11 4 15 15 13 15 15 c 15 11 11 15 14 18
  //   ROM FOR COLUMN 2
  //   --------------------------
  //   |
  //   |
  //   --------------------------
  //   ROM FOR COLUMN 3
  //   --------------------------------------------------------------------------------------------------------------------------------------------------------------------------------------------------------------------------------------------
  //   --------------------------
  //   --------------------------
  //   -------------------------------------------------------------------------------------------------------------------------------------------------------------------------------
  //   contents of rom_3 (hex, n*v repeats v):
  //   11 1f 13 15 4 15 15 14 15 15 14 15 11 11 15 14 1d
  //   |
  //   |
  //   -------------------------------------------------------------------------------------------------------------------------------------------------------------------------------
  //   ROM FOR COLUMN 4
  //   -------------------------------------------------------------------------------------------------------------------------------------------------------------------------------
  //   LED MATRIX
  //    (OUTPUT)
  //   contents of rom_4 (hex, n*v repeats v):
  //   e 1 15 15 1f 15 15 18 15 15 c d 11 a 11 10 18
  //   -
  //   ROM FOR COLUMN 5
  //   |
  //   contents of rom_5 (hex, n*v repeats v):
  //   0 1 9 a 4 12 12 10 a e 7 2 a 4 11 10
  //   |
  //   |
  //   -
endmodule

module LED_Connector (
  input  [4:0] in_1,
  output out_2,
  output out_3,
  output out_4,
  output out_5,
  output out_6
);


  assign out_2 = in_1[4];
  assign out_3 = in_1[3];
  assign out_4 = in_1[2];
  assign out_5 = in_1[1];
  assign out_6 = in_1[0];
endmodule
